# Fritzing sketch REtest (saved by Fritzing 0.7.5b)
breadboards: 1

parts:
  Arduino1 = Arduino
  RE1 = Rotary Encoder [package=THT]
  R1 = Resistor [tolerance=±5% resistance=4.7k package=THT]
  R2 = Resistor [tolerance=±5% resistance=4.7k package=THT]

nets:
  N1: Arduino1.D3, RE1.EncoderPinB, R1.Pin_1
  N2: Arduino1.D2, RE1.EncoderPinA, R2.Pin_1
  5V: Arduino1.+5V, R1.Pin_0, R2.Pin_0
  GND: RE1.EncoderPinC
