# Fritzing sketch TLC5940 (saved by Fritzing 0.7.5b)
breadboards: 1

parts:
  IC1 = IC, DIP package, 28 pins [chip_label=TLC5940 spacing=300mil]
  Arduino1 = Arduino
  LED1 = LED - 5mm [color="Green (565nm)" package="5 mm [THT]"]
  LED2 = LED - 5mm [color="Green (565nm)" package="5 mm [THT]"]
  LED3 = LED - 5mm [color="Green (565nm)" package="5 mm [THT]"]
  LED4 = LED - 5mm [color="Green (565nm)" package="5 mm [THT]"]
  LED5 = LED - 5mm [color="Green (565nm)" package="5 mm [THT]"]
  LED6 = LED - 5mm [color="Green (565nm)" package="5 mm [THT]"]
  LED7 = LED - 5mm [color="Green (565nm)" package="5 mm [THT]"]
  LED8 = LED - 5mm [color="Green (565nm)" package="5 mm [THT]"]
  LED9 = LED - 5mm [color="Green (565nm)" package="5 mm [THT]"]
  LED10 = LED - 5mm [color="Green (565nm)" package="5 mm [THT]"]
  LED11 = LED - 5mm [color="Green (565nm)" package="5 mm [THT]"]
  LED12 = LED - 5mm [color="Green (565nm)" package="5 mm [THT]"]
  R1 = Resistor [tolerance=±5% resistance=10k package=THT]
  R2 = Resistor [tolerance=±5% resistance=4.7k package=THT]
  R3 = Resistor [tolerance=±5% resistance=4.7k package=THT]

nets:
  N1: IC1.pin1, LED1.cathode
  N2: IC1.pin2, LED2.cathode
  N3: IC1.pin3, LED3.cathode
  N4: IC1.pin4, LED4.cathode
  N5: IC1.pin5, LED5.cathode
  N6: IC1.pin6, LED6.cathode
  N7: IC1.pin7, LED7.cathode
  N8: IC1.pin8, LED8.cathode
  N9: IC1.pin9, LED9.cathode
  N10: IC1.pin10, LED10.cathode
  N11: IC1.pin11, LED11.cathode
  N12: IC1.pin12, LED12.cathode
  N13: IC1.pin18, Arduino1.D1TX
  5V: IC1.pin19, IC1.pin21, Arduino1.+5V, LED1.anode, LED2.anode, LED3.anode, LED4.anode, LED5.anode, LED6.anode, LED7.anode, LED8.anode, LED9.anode, LED10.anode, LED11.anode, LED12.anode, R1.Pin_1
  N14: IC1.pin20, R2.Pin_1, R3.Pin_1
  GND: IC1.pin22, IC1.pin27, Arduino1.GND, R2.Pin_0, R3.Pin_0
  N15: IC1.pin23, Arduino1.D10, R1.Pin_0
  N16: IC1.pin24, Arduino1.D9
  N17: IC1.pin25, Arduino1.D13
  N18: IC1.pin26, Arduino1.D11
